# Fritzing sketch Schema_Thermistance_Capteur (saved by Fritzing 0.9.3b)
breadboards: 1

parts:
  Composant1 = Arduino Uno (Rev3)
  R1 = Resistor [tolerance=±5% resistance=10k package=THT]
  R2 = Temperature Sensor (Thermistor) [thermistor_type=NTC package=THT]  # not connected
  DHT2 = DHT22 Humidity and Temperature Sensor

nets:
  N1: Composant1.A0, R1.Pin_0
  N2: Composant1.D2, DHT2.NULL
  N3: Composant1.5V, R1.Pin_1
  N4: Composant1.GND, DHT2.DATA
